# Fritzing sketch 06_alarm (saved by Fritzing 0.9.3b)
breadboards: 1

parts:
  LED2 = LED - 3mm [color="Red (633nm)" package="3 mm [THT]"]
  R2 = Resistor [tolerance=±5% resistance=330 package=THT]
  M1 = DOIT Esp32 DevKit v1 (30 pins long, 11 pins width) [part_number=ESP32S-PIN30]
  R3 = Resistor [tolerance=±5% resistance=330 package=THT]
  J1 = Piezo Speaker
  S6 = SWITCH-MOMENTARY-2 [package=tactile-pth-12mm]
  R4 = Resistor [tolerance=±5% resistance=330 package=THT]

nets:
  N1: LED2.cathode, J1.pin2
  N2: LED2.anode, R2.Pin_1
  N3: R2.Pin_0, M1.D4
  N4: M1.3V3, R4.Pin_1
  N5: M1.GND, R3.Pin_0, J1.pin1
  N6: M1.D5, R3.Pin_1, S6.1
  N7: S6.2, R4.Pin_0

custom parts:
  DOIT Esp32 DevKit v1 (30 pins long, 11 pins width): The DOIT Esp32 DevKit v1 is one of the development board created by DOIT to evaluate the ESP-WROOM-32 module. It is based on the ESP32 microcontroller that boasts Wifi, Bluetooth, Ethernet and Low Power support all in a single chip. (vanepp) made breadboard work, adjusted pin numbering and labels and reduced size of schematic and cleaned up pcb. This chip is 30pins long (2 x15) and 11 pins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
